# Fritzing sketch Trash-can-circuit-schematic (saved by Fritzing 0.9.3b)
breadboards: 1

parts:
  Arduino_Uno = Arduino Uno (Rev3)
  Grove_Ultrasonic_Ranger = Grove Buzz
  ESP8266-01 = ESP8266 WiFi Module [part_number=ESP8266]

nets:
  N1: Arduino_Uno.D0/RX, ESP8266-01.RXD
  N2: Arduino_Uno.D1/TX, ESP8266-01.TXD
  N3: Arduino_Uno.D7, Grove_Ultrasonic_Ranger.SIG
  GND: Arduino_Uno.RESET, Arduino_Uno.GND, Grove_Ultrasonic_Ranger.GND, ESP8266-01.GND
  3V3: Arduino_Uno.3V3, ESP8266-01.VCC, ESP8266-01.CH_PD
  5V: Arduino_Uno.5V, Grove_Ultrasonic_Ranger.VCC

custom parts:
  ESP8266 WiFi Module: Generic WiFi Module based on the ESP8266 with onboard PCB antenna and UART communications
